// Logisim project SimpleALU.circ as structural Verilog: 4 circuits, main circuit Main
module _8BitALU (
  input  add,
  input  \and ,
  input  \or ,
  input  \xor ,
  input  left_shift,
  input  right_shift,
  input  sub_flag,
  input  enable,
  input  enable_2,
  input  clock,
  input  _0,
  input  rhs,
  input  lhs,
  input  [7:0] bus,
  output [7:0] \output ,
  output carry_out
);

  wire [7:0] adder_1_out, and_1_out, bit_extender_1_out, controlled_buffer_1_out, controlled_buffer_2_out,
       or_1_out, register_1_q, register_2_q, shiftleft_1_out_2, shiftright_1_out_2, xor_1_out, xor_2_out;

  Register register_1 (.D(controlled_buffer_1_out), .en(enable), .Q(register_1_q), .clk(clock), .clr(_0));
  Register register_2 (.D(controlled_buffer_2_out), .en(enable_2), .Q(register_2_q), .clk(clock), .clr(_0));
  assign controlled_buffer_1_out = rhs ? bus : 8'bz;  // Controlled_Buffer controlled_buffer_1
  assign controlled_buffer_2_out = lhs ? bus : 8'bz;  // Controlled_Buffer controlled_buffer_2
  assign bit_extender_1_out = {{7{sub_flag}}, sub_flag};  // Bit_Extender bit_extender_1
  assign xor_1_out = bit_extender_1_out ^ register_1_q;  // XOR_Gate xor_1, 8 bits wide
  assign and_1_out = register_1_q & register_2_q;  // AND_Gate and_1, 8 bits wide
  assign or_1_out = register_1_q | register_2_q;  // OR_Gate or_1, 8 bits wide
  assign xor_2_out = register_1_q ^ register_2_q;  // XOR_Gate xor_2, 8 bits wide
  ShiftLeft shiftleft_1 (.in_1(register_2_q), .out_2(shiftleft_1_out_2));
  ShiftRight shiftright_1 (.in_1(register_2_q), .out_2(shiftright_1_out_2));
  Adder adder_1 (.a(xor_1_out), .b(register_2_q), .out(adder_1_out), .cin(sub_flag), .cout(carry_out));
  assign \output  = add ? adder_1_out : 8'bz;  // Controlled_Buffer controlled_buffer_3
  assign \output  = \and  ? and_1_out : 8'bz;  // Controlled_Buffer controlled_buffer_4
  assign \output  = \or  ? or_1_out : 8'bz;  // Controlled_Buffer controlled_buffer_5
  assign \output  = \xor  ? xor_2_out : 8'bz;  // Controlled_Buffer controlled_buffer_6
  assign \output  = left_shift ? shiftleft_1_out_2 : 8'bz;  // Controlled_Buffer controlled_buffer_7
  assign \output  = right_shift ? shiftright_1_out_2 : 8'bz;  // Controlled_Buffer controlled_buffer_8
endmodule

module ShiftLeft (
  input  [7:0] in_1,
  output [7:0] out_2
);


  assign out_2 = {in_1[6:0], 1'b0};
endmodule

module ShiftRight (
  input  [7:0] in_1,
  output [7:0] out_2
);


  assign out_2 = {1'b0, in_1[7:1]};
endmodule

module Main (
  input  in_1,
  input  in_2,
  input  in_3,
  input  in_4,
  input  in_5,
  input  in_6,
  input  [7:0] in_7,
  input  [7:0] in_8,
  input  in_9,
  output [7:0] out_10,
  output out_11
);

  // _8BitALU 8bitalu_1: pin names not known; wires that end beside it: in_7, in_8, in_1, in_9, in_2, in_3, in_4, in_5, in_6, out_10, out_11
endmodule
